# Fritzing sketch Untitled Sketch 2 (saved by Fritzing 1.0.1rc)
breadboards: 1

parts:
  Mod1 = Raspberry Pi 4B
  M1 = gear-motor
  M2 = gear-motor
  M3 = gear-motor
  M4 = gear-motor
  M5 = gear-motor
  M6 = gear-motor
  BAT1 = 6v battery [package=battery]
  PWM1 = PCA9685 16x12-bit PWM Breakout
  M7 = RioRand LM2596
  S1 = H-Bridge with L298N
  S2 = H-Bridge with L298N
  S3 = H-Bridge with L298N
  J2 = Basic Servo
  J3 = Basic Servo
  J4 = Basic Servo
  J5 = Basic Servo
  J6 = Basic Servo
  J7 = Basic Servo
  M8 = Humidity and Temperature Sensor DHT11
  Sensor1 = Gas Sensor Breakout Board
  Part1 = Adafruit PCF8591 [part_number="Adafruit #4648"]
  MPU-1 = Adafruit MPU6050
  U1 = SUP500F [package=sup500f]
  RFM95W1 = RFM95W LoRa Module
  S4 = Hall Sensor [part_number=WSH130 package=TO92]
  S5 = Hall Sensor [part_number=WSH130 package=TO92]
  S6 = Hall Sensor [part_number=WSH130 package=TO92]
  S7 = Hall Sensor [part_number=WSH130 package=TO92]
  S8 = Hall Sensor [part_number=WSH130 package=TO92]

nets:
  VCC: Mod1.3V3, PWM1.no_name_yet#505, M8.Vcc, Part1.VCC, MPU-1.VCC, RFM95W1.13_3.3V, S4.VCC, S5.VCC, S6.VCC, S7.VCC, S8.VCC
  VCC_2: Mod1.5V, PWM1.no_name_yet#100, PWM1.no_name_yet#101, PWM1.no_name_yet#102, PWM1.no_name_yet#103, PWM1.no_name_yet#104, PWM1.no_name_yet#105, PWM1.no_name_yet#706, M7.Pin_3, J2.vcc, J3.vcc, J4.vcc, J5.vcc, J6.vcc, J7.vcc, Sensor1.5V
  N1: Mod1.GPIO2, PWM1.no_name_yet#504, Part1.SDA, MPU-1.SDA
  N2: Mod1.GPIO3, PWM1.no_name_yet#503, Part1.SCL, MPU-1.SCL
  GND: Mod1.GND, PWM1.no_name_yet#501, PWM1.no_name_yet#701, PWM1.no_name_yet#1000, PWM1.no_name_yet#1001, PWM1.no_name_yet#1002, PWM1.no_name_yet#1003, PWM1.no_name_yet#1004, PWM1.no_name_yet#1005, M7.Pin_4, J2.gnd, J3.gnd, J4.gnd, J5.gnd, J6.gnd, J7.gnd, M8.GND, Sensor1.GND, Part1.GND, MPU-1.GND, U1.GND, RFM95W1.1_GND, RFM95W1.10_GND, S4.GND, S5.GND, S6.GND, S7.GND, S8.GND
  N3: Mod1.GPIO14, U1.TX-O
  N4: Mod1.GPIO15, U1.RX-I
  N5: Mod1.GPIO23, S8.OUT
  N6: Mod1.GPIO10, RFM95W1.3_MOSI
  N7: Mod1.GPIO9, RFM95W1.2_MISO
  N8: Mod1.GPIO25, RFM95W1.7_DIO5
  N9: Mod1.GPIO11, RFM95W1.4_SCK
  N10: Mod1.GPIO8, RFM95W1.5_NSS_(CS)
  N11: Mod1.GPIO5, M8.Data
  N12: Mod1.GPIO12, S7.OUT
  N13: Mod1.GPIO13, S1.IN3, S2.IN3, S3.IN3
  N14: Mod1.GPIO19, S1.IN2, S2.IN2, S3.IN2
  N15: Mod1.GPIO16, S6.OUT
  N16: Mod1.GPIO26, S1.IN1, S2.IN1, S3.IN1
  N17: Mod1.GPIO20, S5.OUT
  N18: Mod1.GPIO21, S4.OUT
  N19: M1.pin_1, S1.M2-01
  N20: M1.pin_2, S1.M2-02
  N21: M2.pin_1, S2.M1-02
  N22: M2.pin_2, S2.M1-01
  N23: M3.pin_1, S2.M2-01
  N24: M3.pin_2, S2.M2-02
  N25: M4.pin_1, S3.M1-02
  N26: M4.pin_2, S3.M1-01
  N27: M5.pin_1, S3.M2-02
  N28: M5.pin_2, S3.M2-01
  N29: M6.pin_1, S1.M1-02
  N30: M6.pin_2, S1.M1-01
  GND_2: BAT1.-, M7.Pin_1, S1.GND, S2.GND, S3.GND
  12V: BAT1.+, M7.Pin_2, S1.12V, S2.12V, S3.12V
  N31: PWM1.no_name_yet#0, J2.pulse
  N32: PWM1.no_name_yet#1, J3.pulse
  N33: PWM1.no_name_yet#2, J4.pulse
  N34: PWM1.no_name_yet#3, J5.pulse
  N35: PWM1.no_name_yet#4, J6.pulse
  N36: PWM1.no_name_yet#5, J7.pulse
  N37: PWM1.no_name_yet#6, S1.ENA
  N38: PWM1.no_name_yet#7, S1.ENB
  N39: PWM1.no_name_yet#8, S2.ENA
  N40: PWM1.no_name_yet#9, S2.ENB
  N41: PWM1.no_name_yet#10, S3.ENA
  N42: PWM1.no_name_yet#11, S3.ENB
  N43: S1.IN4, S2.IN4, S3.IN4
  N44: Sensor1.AOUT, Part1.AIN0

custom parts:
  6v battery: 6V lead acid battery 12ah
  H-Bridge with L298N: h-bridge
  Humidity and Temperature Sensor DHT11: Digital relative humidity & temperature sensor DHT11
  Gas Sensor Breakout Board: Gas sensor breakout board. Input voltage is 5V. Sensor output is available in analog and digital.
  Adafruit PCF8591: Measuring voltage and adjusting it is what electronics is all about so you won’t get far without friends like the PCF8591 ADC+DAC combo. Analog to Digital Converters help by measuring an analog voltage and turning it into something a microcontroller like a Metro or Arduino can understand. If you’re using a single board computer like a Raspberry Pi, you might not have any other way to measure a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
  Adafruit MPU6050: The MPU-6050 is a popular six axis accelerometer and gyroscope (gyro) that has all the info you need on how things are shakin' and spinnin' . With six axes of sensing and 16-bit measurements, you'll have everything you need to give your robot friend an inner ear. This combination of gyroscopes and accelerometers is commonly referred to as an Inertial Measurement Unit or IMU. Not so long ago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
  SUP500F: SUP500F Venus GPS
  RFM95W LoRa Module: RF Transceiver by Hope RF. Well supported Arduino libraries are available. This Low Power Long Range Transceiver Module for the frequencies 868MHz and 915MHz and it is also available in other versions. This particular part is set for trhough hole rather than SMD in pcb view.
  Hall Sensor: A Hall Sensor
